// Logisim project CU.circ as structural Verilog: 1 circuit, main circuit main
module main (
  input  MOV,
  input  MOI,
  input  LOAD,
  input  STORE,
  input  ADD,
  input  ADI,
  input  SUB,
  input  SUI,
  input  AND,
  input  ANI,
  input  OR,
  input  ORI,
  input  HLT,
  input  CLK,
  output STAGE_1,
  output STAGE_2,
  output STAGE_3,
  output STAGE_4,
  output STAGE_5
);

  wire ENABLE_IR, or_1_out;
  wire [2:0] counter_1_q;

  or or_1 (or_1_out, MOV, MOI, LOAD, STORE, ADD, ADI, SUB, SUI, AND, ANI, OR, ORI);
  and and_1 (ENABLE_IR, STAGE_1, or_1_out);
  Counter #(.width(3), .max('h4)) counter_1 (.D(3'b000), .Q(counter_1_q), .clk(CLK));  // open: load, count, carry, clr
  Decoder #(.select(3), .enable("false")) decoder_1 (
    .out0(STAGE_1), .out1(STAGE_2), .out2(STAGE_3), .out3(STAGE_4), .out4(STAGE_5), .sel(counter_1_q));  // open: out5, out6, out7

  // Other names for the same wires on the sheet: ENABLE_PC = ENABLE_IR

  // Notes on the sheet:
  //   STAGE 1
  //   STAGE COUNTER
endmodule
