// Logisim project miniCPU.circ as structural Verilog: 2 circuits, main circuit main
module main (
  input  CLK,
  input  MOV,
  input  MOI,
  input  LOAD,
  input  STORE,
  input  ADD,
  input  ADI,
  input  SUB,
  input  SUI,
  input  AND,
  input  ANI,
  input  OR,
  input  ORI,
  input  HLT,
  output ENABLE_RA,
  output ENABLE_RB,
  output STAGE_1,
  output ENABLE_SELECT_RA,
  output STAGE_2,
  output ENABLE_SELECT_RB,
  output STAGE_3,
  output ENABLE_ALU,
  output ENABLE_MUX_B,
  output STAGE_4,
  output SELECT_MUX_B,
  output STAGE_5,
  output ENABLE_RM,
  output ENABLE_MUX_Y,
  output ENABLE_RY
);

  wire ENABLE_IR, ENABLE_SELECT_RY, or_1_out, or_2_out, or_3_out, or_4_out, or_5_out, or_6_out, or_7_out,
       or_8_out, SELECT_MUX_MEM, SELECT_MUX_Y, WRITE_MEM;
  wire [2:0] counter_1_q;

  or or_1 (or_1_out, MOV, MOI, LOAD, STORE, ADD, ADI, SUB, SUI, AND, ANI, OR, ORI);
  or or_2 (or_2_out, MOV, MOI, LOAD, STORE, ADD, ADI, SUB, SUI, AND, ANI, OR, ORI);
  or or_3 (or_3_out, MOI, LOAD, STORE, ADI, SUI, ANI, ORI);
  and and_1 (ENABLE_IR, STAGE_1, or_1_out);
  and and_2 (ENABLE_ALU, STAGE_3, or_2_out);
  and and_3 (SELECT_MUX_B, STAGE_3, or_3_out);
  and and_4 (ENABLE_RM, STAGE_3, STORE);
  Counter #(.width(3), .max('h4)) counter_1 (.D(3'b000), .Q(counter_1_q), .clk(CLK));  // open: load, count, carry, clr
  Decoder #(.select(3), .enable("false")) decoder_1 (
    .out0(STAGE_1), .out1(STAGE_2), .out2(STAGE_3), .out3(STAGE_4), .out4(STAGE_5), .sel(counter_1_q));  // open: out5, out6, out7
  or or_4 (or_4_out, STORE, ADD, SUB, AND, OR);
  or or_5 (or_5_out, MOV, MOI, LOAD, STORE, ADD, ADI, SUB, SUI, AND, ANI, OR, ORI);
  or or_6 (or_6_out, STORE, LOAD);
  or or_7 (or_7_out, or_4_out, MOV, LOAD, ADI, SUI, ANI, ORI);
  and and_5 (ENABLE_RB, STAGE_2, or_4_out);
  and and_6 (ENABLE_MUX_Y, STAGE_1, or_5_out);
  and and_7 (SELECT_MUX_MEM, STAGE_4, or_6_out);
  and and_8 (SELECT_MUX_Y, STAGE_4, LOAD);
  and and_9 (WRITE_MEM, STAGE_4, STORE);
  and and_10 (ENABLE_RA, or_7_out, STAGE_2);
  or or_8 (or_8_out, MOV, MOI, LOAD, STORE, ADD, ADI, SUB, SUI, AND, ANI, OR, ORI);
  and and_11 (ENABLE_SELECT_RY, STAGE_5, or_8_out);

  assign ENABLE_MUX_B = ENABLE_ALU;
  assign ENABLE_RY = ENABLE_MUX_Y;
  assign ENABLE_SELECT_RA = ENABLE_RA;
  assign ENABLE_SELECT_RB = ENABLE_RB;

  // Other names for the same wires on the sheet: ENABLE_PC = ENABLE_IR; ENABLE_RZ = ENABLE_ALU

  // Notes on the sheet:
  //   INSTRUCTIONS TO USE
  //   STAGE 1
  //   STAGE 3
  //   STAGE COUNTER
  //   STAGE 4
  //   SIGNALS
  //   STAGE 2
  //   STAGE 5
endmodule

module ALU (
  input  [31:0] Ra,
  input  [31:0] Rb,
  input  [2:0] OP_TYPE,
  input  ALU_ENABLE,
  output [31:0] Rz
);

  wire [31:0] adder_1_out, and_1_out, or_1_out, subtractor_1_out;

  Adder #(.width(32)) adder_1 (.a(Ra), .b(Rb), .out(adder_1_out));  // open: cin, cout
  Subtractor #(.width(32)) subtractor_1 (.a(Ra), .b(Rb), .out(subtractor_1_out));  // open: bin, bout
  Multiplexer #(.select(3), .width(32)) multiplexer_1 (
    .in0(Ra), .in1(adder_1_out), .in2(subtractor_1_out), .in3(and_1_out), .in4(or_1_out), .in5(Rb), .out(Rz),
    .sel(OP_TYPE), .en(ALU_ENABLE));  // open: in6, in7
  assign and_1_out = Rb & Ra;  // AND_Gate and_1, 32 bits wide
  assign or_1_out = Ra | Rb;  // OR_Gate or_1, 32 bits wide

  // Notes on the sheet:
  //   0 for Ra bypass
  //   1 for add Ra+Rb
  //   2 for Ra-Rb
  //   3 for Ra & Rb
  //   4 for Ra | Rb
  //   5 for Rb bypass
endmodule
